// Logisim project CPU.circ as structural Verilog: 35 circuits, main circuit main
module main (
  input  Reset,
  input  [7:0] RAM_Addr_Monitor,
  input  Monitor_Mode,
  input  Storage_Mode
);

  wire bit_extender_1_out, bit_extender_2_out, bit_extender_3_out, bit_extender_4_out, bit_extender_5_out,
       bit_extender_6_out, bit_extender_7_out, bit_extender_8_out, button_1_out, clock_1_out,
       comparator_1_eq, control_unit_1_alu_store, control_unit_1_hlt, control_unit_1_inc,
       control_unit_1_inc_b, control_unit_1_ir_load, control_unit_1_jz_out, control_unit_1_pc_inc,
       control_unit_1_pc_load, control_unit_1_ram_re, control_unit_1_ram_we, control_unit_1_rega_load,
       control_unit_1_regb_load, control_unit_1_vram_we_b, d_ff_1_q, LED, not_1_out, not_2_out, or_1_out,
       or_2_out, register_1_q, register_2_q, rgb_video_1_p3, rgbled_1_p1, rgbled_1_p2, rgbled_11_p1,
       storage_1_done;
  wire [2:0] control_unit_1_alu_op;
  wire [3:0] instructionregister_1_operand, instructionregister_1_operand_2, rgb_video_1_p4, rgb_video_1_p5,
       rigester8_2_q, rigester8_2_q_2;
  wire [7:0] adder_1_out, adder_2_out, alu_1_result, instructionregister_1_opcode, multiplexer_2_out,
       multiplexer_3_out, multiplexer_5_out, multiplexer_6_out, multiplexer_7_out, multiplexer_8_out,
       multiplexer_9_out, programcounter_1_pc, ram8_1_out_5, rigester8_1_q;
  wire [15:0] multiplexer_1_out, rom_1_data, storage_1_instruction_1;

  // Probe on control_unit_1_inc
  Adder adder_1 (.a({rigester8_2_q_2, rigester8_2_q}), .b(8'h1), .out(adder_1_out));  // open: cin, cout
  // Probe on bit_extender_6_out
  or or_1 (or_1_out, Reset, d_ff_1_q);
  D_Flip_Flop d_ff_1 (.D(control_unit_1_hlt), .clk(rgbled_1_p2), .Q(d_ff_1_q));  // open: Qn, preset, reset
  ProgramCounter programcounter_1 (
    .CLK(rgbled_1_p2), .Reset(or_1_out), .Inc(control_unit_1_pc_inc),
    .D({instructionregister_1_operand_2, instructionregister_1_operand}), .Load(rgbled_1_p1),
    .PC(programcounter_1_pc));
  not not_1 (not_1_out, d_ff_1_q);
  Storage storage_1 (
    .Address(programcounter_1_pc), .Reset(button_1_out), .Next_1(not_1_out),
    .Instruction_1(storage_1_instruction_1), .Done(storage_1_done));
  Multiplexer #(.width(16)) multiplexer_1 (
    .in0(storage_1_instruction_1), .in1(rom_1_data), .out(multiplexer_1_out), .sel(Storage_Mode));
  // RGBLED rgbled_1: pin names not known; wires that end beside it: rgbled_1_p1, rgbled_1_p2, rgbled_1_p2
  // RGBLED rgbled_2: pin names not known; wires that end beside it: rgbled_1_p2
  // RGBLED rgbled_3: pin names not known; wires that end beside it: rgbled_1_p2
  // RGBLED rgbled_4: pin names not known; wires that end beside it: rgbled_1_p2
  Rigester8 rigester8_1 (
    .D(multiplexer_5_out), .CLK(rgbled_1_p2), .Reset(or_1_out), .Load(control_unit_1_regb_load),
    .Q(rigester8_1_q));
  ALU alu_1 (
    .A({rigester8_2_q_2, rigester8_2_q}), .B(rigester8_1_q), .Op(control_unit_1_alu_op), .Result(alu_1_result));  // open: out_4
  // RGBLED rgbled_5: pin names not known; wires that end beside it: rgbled_1_p2
  // RGBLED rgbled_6: pin names not known; wires that end beside it: rgbled_1_p2
  // RGBLED rgbled_7: pin names not known; wires that end beside it: rgbled_1_p2
  // RGBLED rgbled_8: pin names not known; wires that end beside it: rgbled_1_p2
  InstructionRegister instructionregister_1 (
    .Instruction(multiplexer_1_out), .Load(control_unit_1_ir_load), .CLK(rgbled_1_p2), .Reset(or_1_out),
    .Operand({instructionregister_1_operand_2, instructionregister_1_operand}),
    .Opcode(instructionregister_1_opcode));
  // RGBLED rgbled_9: pin names not known; wires that end beside it: rgbled_1_p2
  // RGBLED rgbled_10: pin names not known; wires that end beside it: rgbled_1_p2
  // RGBLED rgbled_11: pin names not known; wires that end beside it: rgbled_11_p1, rgbled_11_p1, rgbled_1_p2
  // RGBLED rgbled_12: pin names not known; wires that end beside it: rgbled_1_p2
  LED led_1 (.in(bit_extender_6_out));
  LED led_2 (.in(bit_extender_2_out));
  LED led_3 (.in(bit_extender_1_out));
  ROM #(.dataWidth(16)) rom_1 (.addr(programcounter_1_pc), .data(rom_1_data));
  LedBar #(.matrixcols(1)) ledbar_1 (.led0(rgbled_1_p2));
  LedBar #(.matrixcols(1)) ledbar_2 (.led0(rgbled_1_p2));
  LedBar #(.matrixcols(1)) ledbar_3 (.led0(rgbled_1_p2));
  LedBar #(.matrixcols(1)) ledbar_4 (.led0(rgbled_1_p2));
  LedBar #(.matrixcols(1)) ledbar_5 (.led0(rgbled_1_p2));
  LedBar #(.matrixcols(1)) ledbar_6 (.led0(rgbled_1_p2));
  LedBar #(.matrixcols(1)) ledbar_7 (.led0(rgbled_1_p2));
  LedBar #(.matrixcols(1)) ledbar_8 (.led0(rgbled_1_p2));
  LedBar #(.matrixcols(1)) ledbar_9 (.led0(rgbled_1_p2));
  LedBar #(.matrixcols(1)) ledbar_10 (.led0(rgbled_1_p2));
  LedBar #(.matrixcols(1)) ledbar_11 (.led0(rgbled_1_p2));
  LedBar #(.matrixcols(1)) ledbar_12 (.led0(rgbled_1_p2));
  LedBar #(.matrixcols(1)) ledbar_13 (.led0(rgbled_1_p2));
  LedBar #(.matrixcols(1)) ledbar_14 (.led0(rgbled_1_p2));
  LedBar #(.matrixcols(1)) ledbar_15 (.led0(rgbled_1_p2));
  LedBar #(.matrixcols(1)) ledbar_16 (.led0(rgbled_1_p2));
  LedBar #(.matrixcols(1)) ledbar_17 (.led0(rgbled_1_p2));
  LedBar #(.matrixcols(1)) ledbar_18 (.led0(rgbled_1_p2));
  LedBar #(.matrixcols(1)) ledbar_19 (.led0(rgbled_1_p2));
  LedBar #(.matrixcols(1)) ledbar_20 (.led0(rgbled_1_p2));
  LedBar #(.matrixcols(1)) ledbar_21 (.led0(rgbled_1_p2));
  LedBar #(.matrixcols(1)) ledbar_22 (.led0(rgbled_1_p2));
  // RGBLED rgbled_13: pin names not known; wires that end beside it: rgbled_1_p2
  // RGBLED rgbled_14: pin names not known; wires that end beside it: rgbled_1_p2
  // RGBLED rgbled_15: pin names not known; wires that end beside it: rgbled_1_p2
  // RGBLED rgbled_16: pin names not known; wires that end beside it: rgbled_1_p2
  LED led_4 (.in(bit_extender_8_out));
  LED led_5 (.in(bit_extender_5_out));
  LED led_6 (.in(bit_extender_3_out));
  LED led_7 (.in(bit_extender_3_out));
  // RGBLED rgbled_17: pin names not known; wires that end beside it: rgbled_1_p2, rgbled_1_p2
  // RGBLED rgbled_18: pin names not known; wires that end beside it: rgbled_1_p2
  // RGBLED rgbled_19: pin names not known; wires that end beside it: rgbled_1_p2
  // RGBLED rgbled_20: pin names not known
  LED led_8 (.in(bit_extender_4_out));
  LED led_9 (.in(bit_extender_7_out));
  LED led_10 (.in(LED));
  // RGBLED rgbled_21: pin names not known
  Rigester8 rigester8_2 (
    .D(multiplexer_8_out), .CLK(rgbled_1_p2), .Reset(or_1_out), .Load(or_2_out),
    .Q({rigester8_2_q_2, rigester8_2_q}));
  LedBar #(.matrixcols(1)) ledbar_23 (.led0(rgbled_1_p2));
  LedBar #(.matrixcols(1)) ledbar_24 (.led0(rgbled_1_p2));
  LedBar #(.matrixcols(1)) ledbar_25 (.led0(rgbled_1_p2));
  LedBar #(.matrixcols(1)) ledbar_26 (.led0(rgbled_1_p2));
  LedBar #(.matrixcols(1)) ledbar_27 (.led0(rgbled_1_p2));
  LedBar #(.matrixcols(1)) ledbar_28 (.led0(rgbled_1_p2));
  LedBar #(.matrixcols(1)) ledbar_29 (.led0(rgbled_1_p2));
  LedBar #(.matrixcols(1)) ledbar_30 (.led0(rgbled_1_p2));
  LedBar #(.matrixcols(1)) ledbar_31 (.led0(rgbled_1_p2));
  LedBar #(.matrixcols(1)) ledbar_32 (.led0(rgbled_1_p2));
  LedBar #(.matrixcols(1)) ledbar_33 (.led0(rgbled_1_p2));
  LedBar #(.matrixcols(1)) ledbar_34 (.led0(rgbled_1_p2));
  LedBar #(.matrixcols(1)) ledbar_35 (.led0(rgbled_1_p2));
  LedBar #(.matrixcols(1)) ledbar_36 (.led0(rgbled_1_p2));
  LedBar #(.matrixcols(1)) ledbar_37 (.led0(rgbled_1_p2));
  LedBar #(.matrixcols(1)) ledbar_38 (.led0(rgbled_1_p2));
  LedBar #(.matrixcols(1)) ledbar_39 (.led0(rgbled_1_p2));
  LedBar #(.matrixcols(1)) ledbar_40 (.led0(rgbled_1_p2));
  LedBar #(.matrixcols(1)) ledbar_41 (.led0(rgbled_1_p2));
  LedBar #(.matrixcols(1)) ledbar_42 (.led0(rgbled_1_p2));
  LedBar #(.matrixcols(1)) ledbar_43 (.led0(rgbled_1_p2));
  LedBar #(.matrixcols(1)) ledbar_44 (.led0(rgbled_1_p2));
  Multiplexer #(.width(8)) multiplexer_2 (
    .in0({instructionregister_1_operand_2, instructionregister_1_operand}), .in1(alu_1_result),
    .out(multiplexer_2_out), .sel(control_unit_1_alu_store));
  // RGBLED rgbled_22: pin names not known; wires that end beside it: rgbled_1_p2, rgbled_1_p2
  // RGB_Video #(.height(16), .scale(8), .width(16)) rgb_video_1: pin names not known; wires that end beside it: or_1_out, rgbled_1_p2, rgb_video_1_p3, rgb_video_1_p4, rgb_video_1_p5, {rigester8_2_q_2, rigester8_2_q}
  Bit_Extender #(.out_width(1)) bit_extender_1 (.in(programcounter_1_pc), .out(bit_extender_1_out));
  Bit_Extender #(.out_width(1)) bit_extender_2 (.in({rgb_video_1_p5, rgb_video_1_p4}), .out(bit_extender_2_out));
  and and_1 (rgbled_1_p2, not_2_out, clock_1_out);
  Button button_1 (.out(button_1_out));
  // RGBLED rgbled_23: pin names not known; wires that end beside it: rgbled_1_p2
  // RGBLED rgbled_24: pin names not known
  // RGBLED rgbled_25: pin names not known; wires that end beside it: rgbled_1_p2, rgbled_1_p2
  // RGBLED rgbled_26: pin names not known
  // RGBLED rgbled_27: pin names not known; wires that end beside it: rgbled_1_p2
  // RGBLED rgbled_28: pin names not known; wires that end beside it: rgbled_1_p2
  // RGBLED rgbled_29: pin names not known
  // RGBLED rgbled_30: pin names not known; wires that end beside it: rgbled_1_p2, rgbled_1_p2
  Bit_Extender #(.out_width(1)) bit_extender_3 (.in(multiplexer_2_out), .out(bit_extender_3_out));
  Multiplexer #(.width(8)) multiplexer_3 (
    .in0(adder_1_out), .in1(multiplexer_2_out), .out(multiplexer_3_out), .sel(control_unit_1_inc));
  not not_2 (not_2_out, storage_1_done);
  Clock clock_1 (.out(clock_1_out));
  // RGBLED rgbled_31: pin names not known; wires that end beside it: rgbled_1_p2, {rgb_video_1_p5, rgb_video_1_p4}
  Adder adder_2 (.a(rigester8_1_q), .b(8'h1), .out(adder_2_out));  // open: cin, cout
  Bit_Extender #(.out_width(1)) bit_extender_4 (.in({rigester8_2_q_2, rigester8_2_q}), .out(bit_extender_4_out));
  Bit_Extender #(.out_width(1)) bit_extender_5 (
    .in({instructionregister_1_operand_2, instructionregister_1_operand}), .out(bit_extender_5_out));
  Bit_Extender #(.out_width(1)) bit_extender_6 (.in({rigester8_2_q_2, rigester8_2_q}), .out(bit_extender_6_out));
  Multiplexer #(.width(8)) multiplexer_4 (
    .in0({instructionregister_1_operand_2, instructionregister_1_operand}), .in1(rigester8_1_q),
    .out({rgb_video_1_p5, rgb_video_1_p4}), .sel(control_unit_1_vram_we_b));
  Bit_Extender #(.out_width(1)) bit_extender_7 (.in(multiplexer_5_out), .out(bit_extender_7_out));
  Multiplexer #(.width(8)) multiplexer_5 (
    .in0({instructionregister_1_operand_2, instructionregister_1_operand}), .in1(adder_2_out),
    .out(multiplexer_5_out), .sel(control_unit_1_inc_b));
  Multiplexer #(.width(8)) multiplexer_6 (
    .in0(multiplexer_3_out), .in1({instructionregister_1_operand_2, instructionregister_1_operand}),
    .out(multiplexer_6_out), .sel(control_unit_1_rega_load));
  Multiplexer #(.width(8)) multiplexer_7 (
    .in0(multiplexer_6_out), .in1(ram8_1_out_5), .out(multiplexer_7_out), .sel(register_1_q));
  Multiplexer #(.width(8)) multiplexer_8 (
    .in0(multiplexer_7_out), .in1(ram8_1_out_5), .out(multiplexer_8_out), .sel(register_1_q));
  Multiplexer #(.width(8)) multiplexer_9 (
    .in0({instructionregister_1_operand_2, instructionregister_1_operand}), .in1(RAM_Addr_Monitor),
    .out(multiplexer_9_out), .sel(Monitor_Mode));
  Comparator #(.mode("unsigned")) comparator_1 (
    .a({rigester8_2_q_2, rigester8_2_q}), .b({8{1'b0}}), .eq(comparator_1_eq));  // open: gt, lt
  Hex_Digit_Display hex_digit_display_1 (.value(multiplexer_9_out[3:0]));  // open: dp
  Hex_Digit_Display hex_digit_display_2 (.value(multiplexer_9_out[7:4]));  // open: dp
  Bit_Extender #(.out_width(1)) bit_extender_8 (.in(multiplexer_9_out), .out(bit_extender_8_out));
  Register #(.width(1)) register_1 (
    .D(control_unit_1_ram_re), .en(1'b1), .clk(rgbled_1_p2), .Q(register_1_q), .clr(or_1_out));
  Hex_Digit_Display hex_digit_display_3 (.value(rigester8_2_q));  // open: dp
  Hex_Digit_Display hex_digit_display_4 (.value(rigester8_2_q_2));  // open: dp
  RAM8 ram8_1 (
    .Address(multiplexer_9_out), .WE(control_unit_1_ram_we), .CLK(rgbled_1_p2),
    .DataIn({rigester8_2_q_2, rigester8_2_q}), .out_5(ram8_1_out_5));
  Hex_Digit_Display hex_digit_display_5 (.value(rigester8_2_q));  // open: dp
  Hex_Digit_Display hex_digit_display_6 (.value(rigester8_2_q_2));  // open: dp
  Register #(.width(1)) register_2 (
    .D(control_unit_1_ram_re), .en(1'b1), .clk(rgbled_1_p2), .Q(register_2_q), .clr(or_1_out));
  Hex_Digit_Display hex_digit_display_7 (.value(instructionregister_1_operand));  // open: dp
  Hex_Digit_Display hex_digit_display_8 (.value(instructionregister_1_operand_2));  // open: dp
  or or_2 (or_2_out, register_2_q, control_unit_1_rega_load);
  or or_3 (rgbled_1_p1, control_unit_1_pc_load, control_unit_1_jz_out);
  Control_Unit control_unit_1 (
    .Opcode(instructionregister_1_opcode), .ZeroFlag(comparator_1_eq), .IR_Load(control_unit_1_ir_load),
    .RegB_Load(control_unit_1_regb_load), .ALU_Store(control_unit_1_alu_store),
    .ALU_Op(control_unit_1_alu_op), .HLT(control_unit_1_hlt), .PC_Inc(control_unit_1_pc_inc),
    .RAM_WE(control_unit_1_ram_we), .RegA_Load(control_unit_1_rega_load), .PC_Load(control_unit_1_pc_load),
    .JZ_OUT(control_unit_1_jz_out), .VRAM_WE(LED), .Inc(control_unit_1_inc),
    .VRAM_WE_B(control_unit_1_vram_we_b), .INC_B(control_unit_1_inc_b), .RAM_RE(control_unit_1_ram_re));  // open: Load_B_RAM
  or or_4 (rgb_video_1_p3, LED, control_unit_1_vram_we_b);

  // Notes on the sheet:
  //   Program_Unit
  //   Adder
  //   D-FlipFlop
  //   Reg_B
  //   Storage
  //   MUX
  //   ALU
  //   Instr_Reg
  //   Reg_A
  //   ROM
  //   Nitro-8
  //   AND
  //   Screen
  //   Clock
  //   Adder
  //   MUX
  //   MUX
  //   RAM
  //   Comparter
  //   Reg
  //   Reg
  //   OR
  //   Control_Unit
  //   OR
  //   OR
endmodule

module Full_Adder (
  input  A,
  input  B,
  input  Cin,
  output Sum,
  output Cout
);

  wire and_1_out, and_2_out, xor_1_out;

  xor xor_1 (xor_1_out, A, B);
  and and_1 (and_1_out, Cin, xor_1_out);
  and and_2 (and_2_out, A, B);
  xor xor_2 (Sum, xor_1_out, Cin);
  or or_1 (Cout, and_1_out, and_2_out);

  // Notes on the sheet:
  //   FullAdder
endmodule

module Adder8bit (
  input  B2,
  input  B1,
  input  A0,
  input  B0,
  input  A6,
  input  A2,
  input  A1,
  input  B3,
  input  A7,
  input  B4,
  input  B7,
  input  B5,
  input  B6,
  input  A3,
  input  A5,
  input  A4,
  input  Cin,
  output Cout,
  output S5,
  output S6,
  output S7,
  output S0,
  output S1,
  output S2,
  output S3,
  output S4
);

  wire full_adder_1_cout, full_adder_2_cout, full_adder_3_cout, full_adder_4_cout, full_adder_5_cout,
       full_adder_6_cout, full_adder_7_cout;

  Full_Adder full_adder_1 (.A(A0), .B(B0), .Cin(Cin), .Sum(S0), .Cout(full_adder_1_cout));
  Full_Adder full_adder_2 (.A(A1), .B(B1), .Cin(full_adder_1_cout), .Sum(S1), .Cout(full_adder_2_cout));
  Full_Adder full_adder_3 (.A(A2), .B(B2), .Cin(full_adder_2_cout), .Sum(S2), .Cout(full_adder_3_cout));
  Full_Adder full_adder_4 (.A(A3), .B(B3), .Cin(full_adder_3_cout), .Sum(S3), .Cout(full_adder_4_cout));
  Full_Adder full_adder_5 (.A(A4), .B(B4), .Cin(full_adder_4_cout), .Sum(S4), .Cout(full_adder_5_cout));
  Full_Adder full_adder_6 (.A(A5), .B(B5), .Cin(full_adder_5_cout), .Sum(S5), .Cout(full_adder_6_cout));
  Full_Adder full_adder_7 (.A(A6), .B(B6), .Cin(full_adder_6_cout), .Sum(S6), .Cout(full_adder_7_cout));
  Full_Adder full_adder_8 (.A(A7), .B(B7), .Cin(full_adder_7_cout), .Sum(S7), .Cout(Cout));

  // Notes on the sheet:
  //   Adder8Bit
endmodule

module ALU (
  input  [7:0] A,
  input  [7:0] B,
  input  [2:0] Op,
  output out_4,
  output [7:0] Result
);

  wire [7:0] adder_1_out, and_1_out, not_1_out, or_1_out, shifter_1_out, shifter_2_out, subtractor_1_out,
       xor_1_out;

  Adder adder_1 (.a(A), .b(B), .out(adder_1_out), .cout(out_4));  // open: cin
  Subtractor subtractor_1 (.a(A), .b(B), .out(subtractor_1_out));  // open: bin, bout
  assign and_1_out = A & B;  // AND_Gate and_1, 8 bits wide
  assign xor_1_out = A ^ B;  // XOR_Gate xor_1, 8 bits wide
  assign or_1_out = A | B;  // OR_Gate or_1, 8 bits wide
  assign not_1_out = ~A;  // NOT_Gate not_1, 8 bits wide
  Shifter shifter_1 (.in(A), .\dist (3'b001), .out(shifter_1_out));
  Shifter #(.shift("lr")) shifter_2 (.in(A), .\dist (3'b001), .out(shifter_2_out));
  Multiplexer #(.select(3), .width(8)) multiplexer_1 (
    .in0(adder_1_out), .in1(subtractor_1_out), .in2(and_1_out), .in3(or_1_out), .in4(xor_1_out),
    .in5(not_1_out), .in6(shifter_1_out), .in7(shifter_2_out), .out(Result), .sel(Op));
  Hex_Digit_Display hex_digit_display_1 (.value(Result[7:4]));  // open: dp
  Hex_Digit_Display hex_digit_display_2 (.value(Result[3:0]));  // open: dp

  // Notes on the sheet:
  //   ALU
endmodule

module Rigester8 (
  input  [7:0] D,
  input  CLK,
  input  Reset,
  input  Load,
  output [7:0] Q
);

  Register register_1 (.D(D), .en(Load), .clk(CLK), .Q(Q), .clr(Reset));
  Hex_Digit_Display hex_digit_display_1 (.value(Q[7:4]));  // open: dp
  Hex_Digit_Display hex_digit_display_2 (.value(Q[3:0]));  // open: dp

  // Notes on the sheet:
  //   Register
endmodule

module ProgramCounter (
  input  CLK,
  input  Reset,
  input  Inc,
  input  [7:0] D,
  input  Load,
  output [7:0] PC
);

  wire [7:0] adder_1_out, multiplexer_1_out, multiplexer_2_out;

  Register register_1 (.D(multiplexer_2_out), .en(1'b1), .clk(CLK), .Q(PC), .clr(Reset));
  Hex_Digit_Display hex_digit_display_1 (.value(PC[7:4]));  // open: dp
  Adder adder_1 (.a(PC), .b(8'h1), .out(adder_1_out));  // open: cin, cout
  Hex_Digit_Display hex_digit_display_2 (.value(PC[3:0]));  // open: dp
  Multiplexer #(.width(8)) multiplexer_1 (.in0(PC), .in1(adder_1_out), .out(multiplexer_1_out), .sel(Inc));
  Multiplexer #(.width(8)) multiplexer_2 (.in0(multiplexer_1_out), .in1(D), .out(multiplexer_2_out), .sel(Load));

  // Notes on the sheet:
  //   Program Counter
endmodule

module Half_Adder (
  input  [7:0] Opcode,
  input  ZeroFlag,
  output IR_Load,
  output RegB_Load,
  output ALU_Store,
  output [2:0] ALU_Op,
  output HLT,
  output PC_Inc,
  output RAM_WE,
  output RegA_Load,
  output PC_Load,
  output JZ_OUT,
  output VRAM_WE,
  output Inc,
  output VRAM_WE_B,
  output INC_B,
  output RAM_RE,
  output SETBANK
);

  wire comparator_1_eq, comparator_2_eq, comparator_3_eq, comparator_4_eq, comparator_5_eq, comparator_6_eq,
       comparator_10_eq, not_1_out;

  Comparator #(.mode("unsigned")) comparator_1 (.a(Opcode), .b(8'h10), .eq(comparator_1_eq));  // open: gt, lt
  Comparator #(.mode("unsigned")) comparator_2 (.a(Opcode), .b(8'h11), .eq(comparator_2_eq));  // open: gt, lt
  Comparator #(.mode("unsigned")) comparator_3 (.a(Opcode), .b(8'h20), .eq(comparator_3_eq));  // open: gt, lt
  Comparator #(.mode("unsigned")) comparator_4 (.a(Opcode), .b(8'h21), .eq(comparator_4_eq));  // open: gt, lt
  Comparator #(.mode("unsigned")) comparator_5 (.a(Opcode), .b(8'h22), .eq(comparator_5_eq));  // open: gt, lt
  Comparator #(.mode("unsigned")) comparator_6 (.a(Opcode), .b(8'h23), .eq(comparator_6_eq));  // open: gt, lt
  Comparator #(.mode("unsigned")) comparator_7 (.a(Opcode), .b(8'hf0), .eq(HLT));  // open: gt, lt
  Comparator #(.mode("unsigned")) comparator_8 (.a(Opcode), .b(8'h30), .eq(RAM_WE));  // open: gt, lt
  Comparator #(.mode("unsigned")) comparator_9 (.a(Opcode), .b(8'h40), .eq(PC_Load));  // open: gt, lt
  Comparator #(.mode("unsigned")) comparator_10 (.a(Opcode), .b(8'h50), .eq(comparator_10_eq));  // open: gt, lt
  Comparator #(.mode("unsigned")) comparator_11 (.a(Opcode), .b(8'h60), .eq(VRAM_WE));  // open: gt, lt
  Comparator #(.mode("unsigned")) comparator_12 (.a(Opcode), .b(8'h70), .eq(Inc));  // open: gt, lt
  Comparator #(.mode("unsigned")) comparator_13 (.a(Opcode), .b(8'h61), .eq(VRAM_WE_B));  // open: gt, lt
  Comparator #(.mode("unsigned")) comparator_14 (.a(Opcode), .b(8'h71), .eq(INC_B));  // open: gt, lt
  Comparator #(.mode("unsigned")) comparator_15 (.a(Opcode), .b(8'h80), .eq(RAM_RE));  // open: gt, lt
  Comparator #(.mode("unsigned")) comparator_16 (.a(Opcode), .b(8'h90), .eq(SETBANK));  // open: gt, lt
  and and_1 (JZ_OUT, comparator_10_eq, ZeroFlag);
  not not_1 (not_1_out, HLT);
  or or_1 (ALU_Op[0], comparator_4_eq, comparator_6_eq);
  or or_2 (ALU_Op[1], comparator_5_eq, comparator_6_eq);
  and and_2 (PC_Inc, 1'b1, not_1_out);
  or or_3 (ALU_Store, comparator_3_eq, comparator_4_eq, Inc, comparator_5_eq, comparator_6_eq);
  or or_4 (RegB_Load, comparator_2_eq, INC_B);
  or or_5 (RegA_Load, comparator_1_eq, comparator_3_eq, comparator_4_eq, comparator_5_eq, comparator_6_eq, Inc, RAM_RE);

  assign ALU_Op[2] = 1'b0;
  assign IR_Load = 1'b1;
endmodule

module ROM8 (
  input  [7:0] Address,
  output [15:0] Instruction
);

  ROM #(.dataWidth(16)) rom_1 (.addr(Address), .data(Instruction));
  Hex_Digit_Display hex_digit_display_1 (.value(Instruction[15:12]));  // open: dp
  Hex_Digit_Display hex_digit_display_2 (.value(Instruction[7:4]));  // open: dp
  Hex_Digit_Display hex_digit_display_3 (.value(Instruction[11:8]));  // open: dp
  Hex_Digit_Display hex_digit_display_4 (.value(Instruction[3:0]));  // open: dp

  // Notes on the sheet:
  //   ROM
endmodule

module InstructionRegister (
  input  [15:0] Instruction,
  input  Load,
  input  CLK,
  input  Reset,
  output [7:0] Operand,
  output [7:0] Opcode
);

  Register #(.width(16)) register_1 (.D(Instruction), .en(Load), .clk(CLK), .Q({Opcode, Operand}), .clr(Reset));
  Hex_Digit_Display hex_digit_display_1 (.value(Opcode[7:4]));  // open: dp
  Hex_Digit_Display hex_digit_display_2 (.value(Opcode[3:0]));  // open: dp
  Hex_Digit_Display hex_digit_display_3 (.value(Operand[7:4]));  // open: dp
  Hex_Digit_Display hex_digit_display_4 (.value(Operand[3:0]));  // open: dp

  // Notes on the sheet:
  //   Instruction Register
endmodule

module Control_Unit (
  input  [7:0] Opcode,
  input  ZeroFlag,
  output IR_Load,
  output RegB_Load,
  output ALU_Store,
  output [2:0] ALU_Op,
  output HLT,
  output PC_Inc,
  output RAM_WE,
  output RegA_Load,
  output PC_Load,
  output JZ_OUT,
  output VRAM_WE,
  output Inc,
  output VRAM_WE_B,
  output INC_B,
  output RAM_RE,
  output Load_B_RAM
);

  wire comparator_1_eq, comparator_2_eq, comparator_3_eq, comparator_4_eq, comparator_5_eq, comparator_6_eq,
       comparator_10_eq, not_1_out;

  Comparator #(.mode("unsigned")) comparator_1 (.a(Opcode), .b(8'h10), .eq(comparator_1_eq));  // open: gt, lt
  Comparator #(.mode("unsigned")) comparator_2 (.a(Opcode), .b(8'h11), .eq(comparator_2_eq));  // open: gt, lt
  Comparator #(.mode("unsigned")) comparator_3 (.a(Opcode), .b(8'h20), .eq(comparator_3_eq));  // open: gt, lt
  Comparator #(.mode("unsigned")) comparator_4 (.a(Opcode), .b(8'h21), .eq(comparator_4_eq));  // open: gt, lt
  Comparator #(.mode("unsigned")) comparator_5 (.a(Opcode), .b(8'h22), .eq(comparator_5_eq));  // open: gt, lt
  Comparator #(.mode("unsigned")) comparator_6 (.a(Opcode), .b(8'h23), .eq(comparator_6_eq));  // open: gt, lt
  Comparator #(.mode("unsigned")) comparator_7 (.a(Opcode), .b(8'hf0), .eq(HLT));  // open: gt, lt
  Comparator #(.mode("unsigned")) comparator_8 (.a(Opcode), .b(8'h30), .eq(RAM_WE));  // open: gt, lt
  Comparator #(.mode("unsigned")) comparator_9 (.a(Opcode), .b(8'h40), .eq(PC_Load));  // open: gt, lt
  Comparator #(.mode("unsigned")) comparator_10 (.a(Opcode), .b(8'h50), .eq(comparator_10_eq));  // open: gt, lt
  Comparator #(.mode("unsigned")) comparator_11 (.a(Opcode), .b(8'h60), .eq(VRAM_WE));  // open: gt, lt
  Comparator #(.mode("unsigned")) comparator_12 (.a(Opcode), .b(8'h70), .eq(Inc));  // open: gt, lt
  Comparator #(.mode("unsigned")) comparator_13 (.a(Opcode), .b(8'h61), .eq(VRAM_WE_B));  // open: gt, lt
  Comparator #(.mode("unsigned")) comparator_14 (.a(Opcode), .b(8'h71), .eq(INC_B));  // open: gt, lt
  Comparator #(.mode("unsigned")) comparator_15 (.a(Opcode), .b(8'h80), .eq(RAM_RE));  // open: gt, lt
  Comparator #(.mode("unsigned")) comparator_16 (.a(Opcode), .b(8'h81), .eq(Load_B_RAM));  // open: gt, lt
  or or_1 (ALU_Op[0], comparator_4_eq, comparator_6_eq);
  or or_2 (ALU_Op[1], comparator_5_eq, comparator_6_eq);
  not not_1 (not_1_out, HLT);
  or or_3 (RegB_Load, INC_B, comparator_2_eq);
  or or_4 (ALU_Store, comparator_3_eq, comparator_4_eq, Inc, comparator_5_eq, comparator_6_eq);
  and and_1 (PC_Inc, 1'b1, not_1_out);
  or or_5 (RegA_Load, comparator_1_eq, comparator_3_eq, comparator_4_eq, comparator_5_eq, comparator_6_eq, Inc, RAM_RE);
  and and_2 (JZ_OUT, comparator_10_eq, ZeroFlag);

  assign ALU_Op[2] = 1'b0;
  assign IR_Load = 1'b1;

  // Notes on the sheet:
  //   1
  //   2
  //   3
  //   4
  //   5
  //   6
  //   7
  //   8
  //   9
  //   10
  //   11
  //   12
  //   13
  //   14
  //   15
  //   16
  //   Countrol Unit
endmodule

module RAM8 (
  input  [7:0] Address,
  input  WE,
  input  CLK,
  input  [7:0] DataIn,
  output [7:0] out_5
);

  RAM ram_1 (.addr(Address), .we(WE), .oe(1'b1), .clk(CLK), .din(DataIn), .dout(out_5));

  // Notes on the sheet:
  //   RAM
endmodule

module main2 (
  input  Start,
  input  Reset,
  input  [7:0] RAM_Addr_Monitor,
  input  Monitor_Mode,
  input  Storage_Mode
);

  wire clock_1_out, comparator_1_eq, control_unit_1_alu_store, control_unit_1_hlt, control_unit_1_inc,
       control_unit_1_inc_b, control_unit_1_ir_load, control_unit_1_jz_out, control_unit_1_pc_inc,
       control_unit_1_pc_load, control_unit_1_ram_re, control_unit_1_ram_we, control_unit_1_rega_load,
       control_unit_1_regb_load, control_unit_1_vram_we, control_unit_1_vram_we_b, d_ff_1_q, not_1_out,
       not_2_out, or_1_out, or_2_out, or_3_out, register_1_q, register_2_q, rgb_video_1_p4, rgbled_1_p1,
       storage_1_done;
  wire [2:0] control_unit_1_alu_op;
  wire [3:0] rgb_video_1_p5, rgb_video_1_p6;
  wire [7:0] adder_1_out, adder_2_out, alu_1_result, instructionregister_1_opcode,
       instructionregister_1_operand, multiplexer_2_out, multiplexer_3_out, multiplexer_5_out,
       multiplexer_6_out, multiplexer_7_out, multiplexer_8_out, multiplexer_9_out, programcounter_1_pc,
       ram8_1_out_5, rigester8_1_q, rigester8_2_q;
  wire [15:0] multiplexer_1_out, rom_1_data, storage_1_instruction_1;

  // Probe on or_3_out
  or or_1 (or_1_out, Reset, d_ff_1_q);
  Adder adder_1 (.a(rigester8_2_q), .b(8'h1), .out(adder_1_out));  // open: cin, cout
  D_Flip_Flop d_ff_1 (.D(control_unit_1_hlt), .clk(rgbled_1_p1), .Q(d_ff_1_q));  // open: Qn, preset, reset
  ProgramCounter programcounter_1 (
    .CLK(rgbled_1_p1), .Reset(or_1_out), .Inc(control_unit_1_pc_inc), .D(instructionregister_1_operand),
    .Load(or_3_out), .PC(programcounter_1_pc));
  not not_1 (not_1_out, d_ff_1_q);
  Storage storage_1 (
    .Address(programcounter_1_pc), .Reset(Start), .Next_1(not_1_out),
    .Instruction_1(storage_1_instruction_1), .Done(storage_1_done));
  Rigester8 rigester8_1 (
    .D(multiplexer_6_out), .CLK(rgbled_1_p1), .Reset(or_1_out), .Load(control_unit_1_regb_load),
    .Q(rigester8_1_q));
  // Probe on multiplexer_8_out
  Multiplexer #(.width(16)) multiplexer_1 (
    .in0(storage_1_instruction_1), .in1(rom_1_data), .out(multiplexer_1_out), .sel(Storage_Mode));
  // RGBLED rgbled_1: pin names not known; wires that end beside it: rgbled_1_p1, rgbled_1_p1
  // RGBLED rgbled_2: pin names not known; wires that end beside it: rgbled_1_p1
  ALU alu_1 (.A(rigester8_2_q), .B(rigester8_1_q), .Op(control_unit_1_alu_op), .Result(alu_1_result));  // open: out_4
  // RGBLED rgbled_3: pin names not known; wires that end beside it: rgbled_1_p1
  // RGBLED rgbled_4: pin names not known; wires that end beside it: rgbled_1_p1
  // RGBLED rgbled_5: pin names not known; wires that end beside it: rgbled_1_p1
  // RGBLED rgbled_6: pin names not known; wires that end beside it: rgbled_1_p1
  InstructionRegister instructionregister_1 (
    .Instruction(multiplexer_1_out), .Load(control_unit_1_ir_load), .CLK(rgbled_1_p1), .Reset(or_1_out),
    .Operand(instructionregister_1_operand), .Opcode(instructionregister_1_opcode));
  // RGBLED rgbled_7: pin names not known; wires that end beside it: rgbled_1_p1
  // RGBLED rgbled_8: pin names not known; wires that end beside it: rgbled_1_p1
  // RGBLED rgbled_9: pin names not known; wires that end beside it: rgbled_1_p1
  // RGBLED rgbled_10: pin names not known; wires that end beside it: rgbled_1_p1
  ROM #(.dataWidth(16)) rom_1 (.addr(programcounter_1_pc), .data(rom_1_data));
  LedBar #(.matrixcols(1)) ledbar_1 (.led0(rgbled_1_p1));
  LedBar #(.matrixcols(1)) ledbar_2 (.led0(rgbled_1_p1));
  LedBar #(.matrixcols(1)) ledbar_3 (.led0(rgbled_1_p1));
  LedBar #(.matrixcols(1)) ledbar_4 (.led0(rgbled_1_p1));
  LedBar #(.matrixcols(1)) ledbar_5 (.led0(rgbled_1_p1));
  LedBar #(.matrixcols(1)) ledbar_6 (.led0(rgbled_1_p1));
  LedBar #(.matrixcols(1)) ledbar_7 (.led0(rgbled_1_p1));
  LedBar #(.matrixcols(1)) ledbar_8 (.led0(rgbled_1_p1));
  LedBar #(.matrixcols(1)) ledbar_9 (.led0(rgbled_1_p1));
  LedBar #(.matrixcols(1)) ledbar_10 (.led0(rgbled_1_p1));
  LedBar #(.matrixcols(1)) ledbar_11 (.led0(rgbled_1_p1));
  LedBar #(.matrixcols(1)) ledbar_12 (.led0(rgbled_1_p1));
  LedBar #(.matrixcols(1)) ledbar_13 (.led0(rgbled_1_p1));
  LedBar #(.matrixcols(1)) ledbar_14 (.led0(rgbled_1_p1));
  LedBar #(.matrixcols(1)) ledbar_15 (.led0(rgbled_1_p1));
  LedBar #(.matrixcols(1)) ledbar_16 (.led0(rgbled_1_p1));
  LedBar #(.matrixcols(1)) ledbar_17 (.led0(rgbled_1_p1));
  LedBar #(.matrixcols(1)) ledbar_18 (.led0(rgbled_1_p1));
  LedBar #(.matrixcols(1)) ledbar_19 (.led0(rgbled_1_p1));
  LedBar #(.matrixcols(1)) ledbar_20 (.led0(rgbled_1_p1));
  LedBar #(.matrixcols(1)) ledbar_21 (.led0(rgbled_1_p1));
  LedBar #(.matrixcols(1)) ledbar_22 (.led0(rgbled_1_p1));
  // RGBLED rgbled_11: pin names not known; wires that end beside it: rgbled_1_p1
  // RGBLED rgbled_12: pin names not known; wires that end beside it: rgbled_1_p1
  // RGBLED rgbled_13: pin names not known; wires that end beside it: rgbled_1_p1
  // RGBLED rgbled_14: pin names not known; wires that end beside it: rgbled_1_p1
  // RGBLED rgbled_15: pin names not known; wires that end beside it: rgbled_1_p1, rgbled_1_p1
  // RGBLED rgbled_16: pin names not known; wires that end beside it: rgbled_1_p1
  // RGBLED rgbled_17: pin names not known; wires that end beside it: rgbled_1_p1
  // RGBLED rgbled_18: pin names not known
  Rigester8 rigester8_2 (
    .D(multiplexer_8_out), .CLK(rgbled_1_p1), .Reset(or_1_out), .Load(or_2_out), .Q(rigester8_2_q));
  // RGBLED rgbled_19: pin names not known; wires that end beside it: rgbled_1_p1
  // RGBLED rgbled_20: pin names not known; wires that end beside it: rgbled_1_p1
  // RGBLED rgbled_21: pin names not known; wires that end beside it: rgbled_1_p1
  // RGBLED rgbled_22: pin names not known
  LedBar #(.matrixcols(1)) ledbar_23 (.led0(rgbled_1_p1));
  LedBar #(.matrixcols(1)) ledbar_24 (.led0(rgbled_1_p1));
  LedBar #(.matrixcols(1)) ledbar_25 (.led0(rgbled_1_p1));
  LedBar #(.matrixcols(1)) ledbar_26 (.led0(rgbled_1_p1));
  LedBar #(.matrixcols(1)) ledbar_27 (.led0(rgbled_1_p1));
  LedBar #(.matrixcols(1)) ledbar_28 (.led0(rgbled_1_p1));
  LedBar #(.matrixcols(1)) ledbar_29 (.led0(rgbled_1_p1));
  LedBar #(.matrixcols(1)) ledbar_30 (.led0(rgbled_1_p1));
  LedBar #(.matrixcols(1)) ledbar_31 (.led0(rgbled_1_p1));
  LedBar #(.matrixcols(1)) ledbar_32 (.led0(rgbled_1_p1));
  LedBar #(.matrixcols(1)) ledbar_33 (.led0(rgbled_1_p1));
  LedBar #(.matrixcols(1)) ledbar_34 (.led0(rgbled_1_p1));
  LedBar #(.matrixcols(1)) ledbar_35 (.led0(rgbled_1_p1));
  LedBar #(.matrixcols(1)) ledbar_36 (.led0(rgbled_1_p1));
  LedBar #(.matrixcols(1)) ledbar_37 (.led0(rgbled_1_p1));
  LedBar #(.matrixcols(1)) ledbar_38 (.led0(rgbled_1_p1));
  LedBar #(.matrixcols(1)) ledbar_39 (.led0(rgbled_1_p1));
  LedBar #(.matrixcols(1)) ledbar_40 (.led0(rgbled_1_p1));
  LedBar #(.matrixcols(1)) ledbar_41 (.led0(rgbled_1_p1));
  LedBar #(.matrixcols(1)) ledbar_42 (.led0(rgbled_1_p1));
  LedBar #(.matrixcols(1)) ledbar_43 (.led0(rgbled_1_p1));
  LedBar #(.matrixcols(1)) ledbar_44 (.led0(rgbled_1_p1));
  Multiplexer #(.width(8)) multiplexer_2 (
    .in0(instructionregister_1_operand), .in1(alu_1_result), .out(multiplexer_2_out),
    .sel(control_unit_1_alu_store));
  // RGBLED rgbled_23: pin names not known; wires that end beside it: rgbled_1_p1
  // RGB_Video #(.height(16), .scale(8), .width(16)) rgb_video_1: pin names not known; wires that end beside it: or_1_out, or_1_out, rgbled_1_p1, rgb_video_1_p4, rgb_video_1_p5, rgb_video_1_p6, rigester8_2_q
  // Probe on rgb_video_1_p4
  and and_1 (rgbled_1_p1, not_2_out, clock_1_out);
  // RGBLED rgbled_24: pin names not known; wires that end beside it: rgbled_1_p1
  // RGBLED rgbled_25: pin names not known
  // RGBLED rgbled_26: pin names not known; wires that end beside it: rgbled_1_p1, rgbled_1_p1
  // RGBLED rgbled_27: pin names not known
  // RGBLED rgbled_28: pin names not known; wires that end beside it: rgbled_1_p1
  // RGBLED rgbled_29: pin names not known; wires that end beside it: rgbled_1_p1
  // RGBLED rgbled_30: pin names not known
  // RGBLED rgbled_31: pin names not known; wires that end beside it: rgbled_1_p1, rgbled_1_p1
  Multiplexer #(.width(8)) multiplexer_3 (
    .in0(adder_1_out), .in1(multiplexer_2_out), .out(multiplexer_3_out), .sel(control_unit_1_inc));
  Clock clock_1 (.out(clock_1_out));
  not not_2 (not_2_out, storage_1_done);
  // RGBLED rgbled_32: pin names not known; wires that end beside it: rgbled_1_p1
  Adder adder_2 (.a(rigester8_1_q), .b(8'h1), .out(adder_2_out));  // open: cin, cout
  // Probe on control_unit_1_rega_load
  Multiplexer #(.width(8)) multiplexer_4 (
    .in0(instructionregister_1_operand), .in1(rigester8_1_q), .out({rgb_video_1_p6, rgb_video_1_p5}),
    .sel(control_unit_1_vram_we_b));
  Multiplexer #(.width(8)) multiplexer_5 (
    .in0(multiplexer_3_out), .in1(instructionregister_1_operand), .out(multiplexer_5_out),
    .sel(control_unit_1_rega_load));
  Multiplexer #(.width(8)) multiplexer_6 (
    .in0(instructionregister_1_operand), .in1(adder_2_out), .out(multiplexer_6_out),
    .sel(control_unit_1_inc_b));
  Multiplexer #(.width(8)) multiplexer_7 (
    .in0(multiplexer_5_out), .in1(ram8_1_out_5), .out(multiplexer_7_out), .sel(register_1_q));
  // Probe on register_1_q
  Multiplexer #(.width(8)) multiplexer_8 (
    .in0(multiplexer_7_out), .in1(ram8_1_out_5), .out(multiplexer_8_out), .sel(register_1_q));
  Multiplexer #(.width(8)) multiplexer_9 (
    .in0(instructionregister_1_operand), .in1(RAM_Addr_Monitor), .out(multiplexer_9_out), .sel(Monitor_Mode));
  Comparator #(.mode("unsigned")) comparator_1 (
    .a(rigester8_2_q), .b({8{1'b0}}), .eq(comparator_1_eq));  // open: gt, lt
  Register #(.width(1)) register_1 (
    .D(control_unit_1_ram_re), .en(1'b1), .clk(rgbled_1_p1), .Q(register_1_q), .clr(or_1_out));
  RAM8 ram8_1 (
    .Address(multiplexer_9_out), .WE(control_unit_1_ram_we), .CLK(rgbled_1_p1), .DataIn(rigester8_2_q),
    .out_5(ram8_1_out_5));
  Register #(.width(1)) register_2 (
    .D(control_unit_1_ram_re), .en(1'b1), .clk(rgbled_1_p1), .Q(register_2_q), .clr(or_1_out));
  or or_2 (or_2_out, register_2_q, control_unit_1_rega_load);
  or or_3 (or_3_out, control_unit_1_pc_load, control_unit_1_jz_out);
  Control_Unit control_unit_1 (
    .Opcode(instructionregister_1_opcode), .ZeroFlag(comparator_1_eq), .IR_Load(control_unit_1_ir_load),
    .RegB_Load(control_unit_1_regb_load), .ALU_Store(control_unit_1_alu_store),
    .ALU_Op(control_unit_1_alu_op), .HLT(control_unit_1_hlt), .PC_Inc(control_unit_1_pc_inc),
    .RAM_WE(control_unit_1_ram_we), .RegA_Load(control_unit_1_rega_load), .PC_Load(control_unit_1_pc_load),
    .JZ_OUT(control_unit_1_jz_out), .VRAM_WE(control_unit_1_vram_we), .Inc(control_unit_1_inc),
    .VRAM_WE_B(control_unit_1_vram_we_b), .INC_B(control_unit_1_inc_b), .RAM_RE(control_unit_1_ram_re));  // open: Load_B_RAM
  or or_4 (rgb_video_1_p4, control_unit_1_vram_we, control_unit_1_vram_we_b);

  // Notes on the sheet:
  //   OR
  //   Program_Unit
  //   Adder
  //   D-FlipFlop
  //   Reg_B
  //   Storage
  //   MUX
  //   ALU
  //   Instr_Reg
  //   Reg_A
  //   ROM
  //   Nitro-8
  //   MUX
  //   AND
  //   Screen
  //   MUX
  //   Clock
  //   Adder
  //   MUX
  //   MUX
  //   MUX
  //   MUX
  //   MUX
  //   RAM
  //   Comparter
  //   Reg
  //   Reg
  //   OR
  //   Control_Unit
  //   OR
  //   OR
endmodule

module Storage (
  input  [7:0] Address,
  input  Reset,
  input  Next_1,
  output [15:0] Instruction_1,
  output Done
);

  wire counter_1_carry;
  wire [4:0] counter_1_q;
  wire [15:0] unit1_1_instruction, unit2_1_instruction, unit3_1_instruction, unit4_1_instruction,
       unit5_1_instruction, unit6_1_instruction, unit7_1_instruction, unit8_1_instruction,
       unit9_1_instruction, unit10_1_instruction, unit11_1_instruction, unit12_1_instruction,
       unit13_1_instruction, unit14_1_instruction, unit15_1_instruction, unit16_1_instruction,
       unit17_1_instruction, unit18_1_instruction, unit19_1_instruction, unit20_1_instruction;

  Unit1 unit1_1 (.Address(Address), .Instruction(unit1_1_instruction));
  Unit2 unit2_1 (.Address(Address), .Instruction(unit2_1_instruction));
  Unit3 unit3_1 (.Address(Address), .Instruction(unit3_1_instruction));
  Unit4 unit4_1 (.Address(Address), .Instruction(unit4_1_instruction));
  Unit5 unit5_1 (.Address(Address), .Instruction(unit5_1_instruction));
  Unit6 unit6_1 (.Address(Address), .Instruction(unit6_1_instruction));
  Unit7 unit7_1 (.Address(Address), .Instruction(unit7_1_instruction));
  Unit8 unit8_1 (.Address(Address), .Instruction(unit8_1_instruction));
  Unit9 unit9_1 (.Address(Address), .Instruction(unit9_1_instruction));
  Unit10 unit10_1 (.Address(Address), .Instruction(unit10_1_instruction));
  Counter #(.max('h1f), .width(5)) counter_1 (
    .clr(Reset), .load(1'b0), .up(1'b1), .count(1'b1), .clk(Next_1), .carry(counter_1_carry), .Q(counter_1_q));  // open: D
  Unit11 unit11_1 (.Address(Address), .Instruction(unit11_1_instruction));
  Unit12 unit12_1 (.Address(Address), .Instruction(unit12_1_instruction));
  Unit13 unit13_1 (.Address(Address), .Instruction(unit13_1_instruction));
  Unit14 unit14_1 (.Address(Address), .Instruction(unit14_1_instruction));
  Unit15 unit15_1 (.Address(Address), .Instruction(unit15_1_instruction));
  Unit16 unit16_1 (.Address(Address), .Instruction(unit16_1_instruction));
  Unit17 unit17_1 (.Address(Address), .Instruction(unit17_1_instruction));
  Unit18 unit18_1 (.Address(Address), .Instruction(unit18_1_instruction));
  Unit19 unit19_1 (.Address(Address), .Instruction(unit19_1_instruction));
  Unit20 unit20_1 (.Address(Address), .Instruction(unit20_1_instruction));
  Comparator #(.mode("unsigned"), .width(5)) comparator_1 (.a(counter_1_q), .b(5'b10100), .eq(Done));  // open: gt, lt
  Multiplexer #(.select(5), .width(16)) multiplexer_1 (
    .in0(unit1_1_instruction), .in1(unit2_1_instruction), .in2(unit3_1_instruction),
    .in3(unit4_1_instruction), .in4(unit5_1_instruction), .in5(unit6_1_instruction),
    .in6(unit7_1_instruction), .in7(unit8_1_instruction), .in8(unit9_1_instruction),
    .in9(unit10_1_instruction), .in10(unit11_1_instruction), .in11(unit12_1_instruction),
    .in12(unit13_1_instruction), .in13(unit14_1_instruction), .in14(unit15_1_instruction),
    .in15(unit16_1_instruction), .in16(unit17_1_instruction), .in17(unit18_1_instruction),
    .in18(unit19_1_instruction), .in19(unit20_1_instruction), .out(Instruction_1), .sel(counter_1_q));  // open: in20, in21, in22, in23, in24, in25, in26, in27, in28, in29, in30, in31

  // Notes on the sheet:
  //   Storage
endmodule

module Unit2 (
  input  [7:0] Address,
  output [15:0] Instruction
);

  ROM #(.dataWidth(16)) Unit2 (.addr(Address), .data(Instruction));

  // Notes on the sheet:
  //   contents of Unit2 (hex, n*v repeats v):
  //   10d0 0 6033 0 6034 0 6035 0 6036 0 6037 0 6038 0 6039 0 603a 0 603b 0 603c 0 6042 0 604d 0 6052 0
  //   605d 0 6061 0 6062 0 6064 0 6065 0 6066 0 6069 0 606a 0 606b 0 606d 0 606e 0 6071 0 6072 0 6074 0
  //   6076 0 6079 0 607b 0 607d 0 607e 0 6081 0 6082 0 6084 0 6085 0 6086 0 6089 0 608a 0 608b 0 608d 0
  //   608e 0 6091 0 6092 0 609d 0 609e 0 60a2 0 60a5 0 60a6 0 60a7 0 60a8 0 60a9 0 60aa 0 60ad 0 60b2 0
  //   60bd 0 60c3 0 60c4 0 60c5 0 60c6 0 60c7 0 60c8 0 60c9 0 60ca 0 60cb 0 60cc 0 f000
endmodule

module Unit3 (
  input  [7:0] Address,
  output [15:0] Instruction
);

  ROM #(.dataWidth(16)) Unit2 (.addr(Address), .data(Instruction));

  // Notes on the sheet:
  //   contents of Unit2 (hex, n*v repeats v):
  //   10a0 0 6007 0 6016 0 6018 0 6025 0 6029 0 6074 0 607a 0 6083 0 6084 0 608a 0 608b 0 6093 0 609b 0
  //   60a3 0 60ab 0 10ff 0 6017 0 6026 0 6027 0 6028 0 6035 0 6036 0 6037 0 6038 0 6039 0 6045 0 6049 0
  //   6055 0 6059 0 6065 0 6069 0 6075 0 6076 0 6077 0 6078 0 6079 0 6085 0 6086 0 6087 0 6088 0 6089 0
  //   6095 0 6096 0 6097 0 6098 0 6099 0 100c 0 6046 0 6066 0 10f0 0 6047 0 6056 0 6057 0 6067 0 10f8 0
  //   60a5 0 60a6 0 60a7 0 60a8 0 60a9 0 60b5 0 60b9 0 10e3 0 60c6 0 60c7 0 60c8 0 60d6 0 60d7 0 60d8 0
  //   60e7 0 10d0 0 60b6 0 60b7 0 60b8 0 60c5 0 60c9 0 60e6 0 60e8 0 60f7 0 f000
endmodule

module Unit4 (
  input  [7:0] Address,
  output [15:0] Instruction
);

  ROM #(.dataWidth(16)) Unit2 (.addr(Address), .data(Instruction));

  // Notes on the sheet:
  //   contents of Unit2 (hex, n*v repeats v):
  //   10a0 0 6017 0 10c3 0 6046 0 6055 0 10f0 0 6027 0 6036 0 6037 0 6038 0 6045 0 6049 0 6072 0 6073 0
  //   6074 0 6075 0 6076 0 6077 0 6078 0 6079 0 607a 0 607b 0 607c 0 6081 0 6082 0 6084 0 6086 0 6088 0
  //   608a 0 608c 0 608d 0 6092 0 6093 0 6094 0 6095 0 6096 0 6097 0 6098 0 6099 0 609a 0 609b 609c 60a3 0
  //   60a4 0 60a5 0 60a6 0 60a7 0 60a8 0 60a9 0 100c 0 6045 0 6047 0 6048 0 6049 0 6053 6054 6056 0 6057 0
  //   6058 0 6059 0 605a 0 605b 0 6063 0 6064 0 6065 0 6066 0 6067 0 6068 0 6069 0 606a 0 606b 0 1024 0
  //   6083 0 6085 0 6087 0 6089 0 608b 0 10d0 0 60b6 0 60b8 0 60c6 0 60c8 0 60d5 0 60d9 0 60e5 0 60e9 0
  //   60f4 0 60fa 0 10e3 0 60b7 0 60c7 0 60d6 0 60d7 0 60d8 0 60e6 0 60e7 0 60e8 0 60f5 0 60f6 0 60f7 0
  //   60f8 0 60f9 0 f000
endmodule

module Unit5 (
  input  [7:0] Address,
  output [15:0] Instruction
);

  ROM #(.dataWidth(16)) Unit2 (.addr(Address), .data(Instruction));

  // Notes on the sheet:
  //   contents of Unit2 (hex, n*v repeats v):
  //   10a0 0 6015 0 6025 0 6026 0 6035 0 6036 0 6038 0 6039 0 10c3 0 6056 0 100c 0 6027 0 6037 0 6045 0
  //   6046 0 6047 0 6048 0 6049 0 6057 0 1024 0 6043 0 6044 0 6045 0 6048 0 6049 0 604a 0 6052 0 6053 0
  //   6055 0 6057 0 6058 0 6059 0 6062 0 6063 0 6064 0 6065 0 6066 0 6067 0 6068 0 6069 0 606a 0 6073 0
  //   6074 0 6075 0 6076 0 6077 0 6078 0 6079 0 6084 0 6085 0 6086 0 6087 0 6088 0 6093 0 6094 0 6095 0
  //   6096 0 6097 0 60a2 0 60a3 0 60a4 0 60a6 0 60a7 0 60a8 0 60b3 0 60b4 0 60b5 0 60b6 0 60b7 0 60c4 0
  //   60c7 0 10e3 0 60a5 0 60a6 0 60b5 0 60b6 0 f000
endmodule

module Unit6 (
  input  [7:0] Address,
  output [15:0] Instruction
);

  ROM #(.dataWidth(16)) Unit2 (.addr(Address), .data(Instruction));

  // Notes on the sheet:
  //   contents of Unit2 (hex, n*v repeats v):
  //   10a8 0 6037 0 6046 0 6047 0 6048 0 6055 0 6056 0 6057 0 6058 0 6059 0 6066 0 6067 0 6068 0 10c3 0
  //   6047 0 10a0 0 6059 0 6065 0 6069 0 6077 0 1034 0 6077 0 6087 0 6097 0 60a7 0 60b7 0 60c7 0 60d7 0
  //   1030 0 60a5 0 60a6 0 60a8 0 60a9 0 60b4 0 60b5 0 60b6 0 60b7 0 60b8 0 60b9 0 60c3 0 60c4 0 60c5 0
  //   60c6 0 60c8 0 60c9 0 f000
endmodule

module Unit1 (
  input  [7:0] Address,
  output [15:0] Instruction
);

  ROM #(.dataWidth(16)) rom_1 (.addr(Address), .data(Instruction));

  // Notes on the sheet:
  //   contents of rom_1 (hex, n*v repeats v):
  //   10a0 0 6033 0 6034 0 6037 0 6038 0 603b 0 603c 0 6043 0 6044 0 6047 0 6048 0 604b 0 604c 0 6053 0
  //   6054 0 6057 0 6058 0 6063 0 6064 0 6067 0 6068 0 606b 0 606c 0 6073 0 6074 0 6075 0 6076 0 6077 0
  //   6078 0 607b 0 607c 0 6083 0 6084 0 6085 0 6086 0 6087 0 6088 0 608b 0 608c 0 6093 0 6094 0 6097 0
  //   6098 0 609b 0 609c 0 60a3 0 60a4 0 60a7 0 60a8 0 60ab 0 60ac 0 60b3 0 60b4 0 60b7 0 60b8 0 60bb 0
  //   60bc 0 60c3 0 60c4 0 60c7 0 60c8 0 60cb 0 60cc 0 f000
endmodule

module Unit7 (
  input  [7:0] Address,
  output [15:0] Instruction
);

  ROM #(.dataWidth(16)) Unit2 (.addr(Address), .data(Instruction));

  // Notes on the sheet:
  //   contents of Unit2 (hex, n*v repeats v):
  //   1050 0 6018 0 6028 0 6037 0 6038 0 6039 0 6046 0 6047 0 6048 0 6049 0 604a 0 6055 0 6056 0 6057 0
  //   6058 0 6059 0 605a 0 605b 0 6061 0 6062 0 6063 0 6064 0 6065 0 6066 0 6067 0 6068 0 6069 0 606a 0
  //   606b 0 606c 0 606d 0 606e 0 606f 0 6072 0 6073 0 6074 0 6075 0 6076 0 6077 0 6078 0 6079 0 607a 0
  //   607b 0 607c 0 607d 0 607e 0 6083 0 6084 0 6085 0 6086 0 6087 0 6088 0 6089 0 608a 0 608b 0 608c 0
  //   608d 0 6094 0 6095 0 6096 0 6097 0 6098 0 6099 0 609a 0 609b 0 609c 0 60a5 0 60a6 0 60a7 0 60a8 0
  //   60a9 0 60aa 0 60ab 0 60b5 0 60b6 0 60b7 0 60b8 0 60b9 0 60ba 0 60bb 0 60c4 0 60c5 0 60c6 0 60c7 0
  //   60c9 0 60ca 0 60cb 0 60cc 0 60d4 0 60d5 0 60d6 0 60da 0 60db 0 60dc 0 60e4 0 60e5 0 60eb 0 60ec 0
  //   60f4 0 60fc 0 f000
endmodule

module Unit8 (
  input  [7:0] Address,
  output [15:0] Instruction
);

  ROM #(.dataWidth(16)) Unit2 (.addr(Address), .data(Instruction));

  // Notes on the sheet:
  //   contents of Unit2 (hex, n*v repeats v):
  //   10e3 0 6035 0 6036 0 6037 0 6038 0 6039 0 6044 0 6045 0 6046 0 6047 0 6048 0 6049 0 604a 0 6053 0
  //   6054 0 6055 0 6056 0 6057 0 6058 0 6059 0 605a 0 605b 0 6062 0 6063 0 6064 0 6065 0 6066 0 6067 0
  //   6068 0 6069 0 606a 0 606b 0 606c 0 6072 0 6073 0 6074 0 6075 0 6076 0 6077 0 6078 0 6079 0 607a 0
  //   607b 0 607c 0 6083 0 6084 0 6085 0 6086 0 6087 0 6088 0 6089 0 608a 0 608b 0 6094 0 6095 0 6096 0
  //   6097 0 6098 0 6099 0 609a 0 60a5 0 60a6 0 60a7 0 60a8 0 60a9 0 10c3 0 6055 0 6059 0 10a0 0 6085 0
  //   6086 0 6087 0 6088 0 6089 0 6094 0 609a 0 f000
endmodule

module Unit9 (
  input  [7:0] Address,
  output [15:0] Instruction
);

  ROM #(.dataWidth(16)) Unit2 (.addr(Address), .data(Instruction));

  // Notes on the sheet:
  //   contents of Unit2 (hex, n*v repeats v):
  //   10d0 0 6034 0 6035 0 6036 0 6037 0 6038 0 6039 0 603a 0 603b 0 6043 0 6044 0 6045 0 604a 0 604b 0
  //   604c 0 6052 0 6053 0 6054 0 6055 0 605a 0 605b 0 605c 0 605d 0 6062 0 6063 0 6064 0 6065 0 6066 0
  //   6067 0 6068 0 6069 0 606a 0 606b 0 606c 0 606d 0 6073 0 6074 0 6075 0 6076 0 6077 0 6078 0 6079 0
  //   607a 0 607b 0 607c 0 6085 0 6086 0 6087 0 6088 0 6089 0 608a 0 102c 0 6046 0 6047 0 6048 0 6049 0
  //   6056 0 6057 0 6058 0 6059 0 10a0 0 6082 0 6083 0 6084 0 608b 0 608c 0 608d 0 10c3 0 6072 0 607d 0
  //   f000
endmodule

module Unit10 (
  input  [7:0] Address,
  output [15:0] Instruction
);

  ROM #(.dataWidth(16)) Unit2 (.addr(Address), .data(Instruction));

  // Notes on the sheet:
  //   contents of Unit2 (hex, n*v repeats v):
  //   1048 0 6013 0 6014 0 6022 0 6023 0 6024 0 602b 0 6031 0 6032 0 6033 0 6034 0 603b 0 603c 0 6042 0
  //   6043 0 6044 0 604b 0 6053 0 6054 0 6064 0 6094 0 60a3 0 60a4 0 60b2 0 60b3 0 60b4 0 60bb 0 60c1 0
  //   60c2 0 60c3 0 60c4 0 60cb 0 60cc 0 60d2 0 60d3 0 60d4 0 60db 0 60e3 0 60e4 0 102c 0 6019 0 601a 0
  //   6025 0 6029 0 602a 0 6035 0 6039 0 603a 0 6045 0 6046 0 6049 0 604a 0 6055 0 6056 0 6065 0 6066 0
  //   6075 0 6076 0 6085 0 6086 0 6095 0 6096 0 60a5 0 60a6 0 60b5 0 60b6 0 60b9 0 60ba 0 60c5 0 60c9 0
  //   60ca 0 60d5 0 60d9 0 60da 0 60e9 0 60ea 0 10c3 0 6028 0 6038 0 6047 0 6048 0 6057 0 6058 0 6067 0
  //   6097 0 60a7 0 60a8 0 60b7 0 60b8 0 60c8 0 60d8 0 f000
endmodule

module Unit11 (
  input  [7:0] Address,
  output [15:0] Instruction
);

  ROM #(.dataWidth(16)) rom_1 (.addr(Address), .data(Instruction));

  // Notes on the sheet:
  //   contents of rom_1 (hex, n*v repeats v):
  //   102c 0 6007 0 6016 0 6017 0 6025 0 6026 0 6034 0 6035 0 6043 0 6044 0 6045 0 6046 0 6047 0 6048 0
  //   6055 0 6056 0 6064 0 0 0 6073 0 6074 0 6082 0 6083 0 6084 0 6085 0 6086 0 6087 0 6094 0 6095 0 60a3
  //   0 60a4 0 60b2 0 60b3 0 60c1 0 60c2 0 60d0 0 60d1 0 f000
endmodule

module Unit12 (
  input  [7:0] Address,
  output [15:0] Instruction
);

  ROM #(.dataWidth(16)) rom_1 (.addr(Address), .data(Instruction));

  // Notes on the sheet:
  //   contents of rom_1 (hex, n*v repeats v):
  //   1030 0 6015 0 6016 0 6017 0 6018 0 6023 0 6024 0 6025 0 6026 0 6027 0 6028 0 6029 0 602a 0 6032 0
  //   6033 0 6034 0 6038 0 6039 0 603a 0 603b 0 6041 0 6042 0 6043 0 604a 0 604b 0 604c 0 6051 0 6052 0
  //   6053 0 605a 0 605b 0 605c 0 6061 0 6062 0 6063 0 6064 0 6065 0 6066 0 6067 0 6068 0 6069 0 606a 0
  //   606b 0 606c 0 6071 0 6072 0 6073 0 6079 0 607a 0 607b 0 6082 0 6083 0 6084 0 6088 0 6089 0 608a 0
  //   6093 0 6094 0 6095 0 6096 0 6097 0 6098 0 60a4 0 60a5 0 60a6 0 60a7 0 60b5 0 60b6 0 10a0 0 6035 0
  //   6036 0 6037 0 6044 0 6048 0 6049 0 6054 0 6055 0 6057 0 6058 0 6059 0 6074 0 6075 0 6076 0 6077 0
  //   6078 0 6085 0 6086 0 6087 0 10c3 0 6045 0 6046 0 6047 0 6056 0 f000
endmodule

module Unit13 (
  input  [7:0] Address,
  output [15:0] Instruction
);

  ROM #(.dataWidth(16)) rom_1 (.addr(Address), .data(Instruction));

  // Notes on the sheet:
  //   contents of rom_1 (hex, n*v repeats v):
  //   10a0 0 6017 0 6026 0 6027 0 6028 0 6035 0 6036 0 6038 0 6039 0 6044 0 6045 0 6049 0 604a 0 6053 0
  //   6054 0 605a 0 605b 0 6062 0 6063 0 606b 0 606c 0 6071 0 6072 0 607c 0 6082 0 6083 0 608b 0 6093 0
  //   6094 0 6099 0 609a 0 60a4 0 60a5 0 60a8 0 60a9 0 60b5 0 60b8 0 60c6 0 60c7 0 60d7 0 10e3 0 6037 0
  //   6046 0 6047 0 6048 0 6055 0 6056 0 6057 0 6058 0 6059 0 6064 0 6065 0 6066 0 6068 0 6069 0 606a 0
  //   6073 0 6074 0 6075 0 6076 0 6077 0 6078 0 6079 0 607a 0 607b 0 6084 0 6085 0 6086 0 6087 0 6088 0
  //   6089 0 608a 0 6095 0 6096 0 6097 0 6098 0 60a6 0 60a7 0 60b6 0 60b7 0 10c3 0 6067 0 f000
endmodule

module Unit14 (
  input  [7:0] Address,
  output [15:0] Instruction
);

  ROM #(.dataWidth(16)) rom_1 (.addr(Address), .data(Instruction));

  // Notes on the sheet:
  //   contents of rom_1 (hex, n*v repeats v):
  //   1030 0 6016 0 6017 0 6018 0 6024 0 6025 0 6026 0 6027 0 6028 0 6029 0 602a 0 6033 0 6034 0 6035 0
  //   6036 0 6037 0 6038 0 6039 0 603a 0 603b 0 6042 0 6043 0 6044 0 6045 0 6046 0 6047 0 6048 0 6049 0
  //   604a 0 604b 0 604c 0 6053 0 6054 0 6055 0 6056 0 6057 0 6058 0 6059 0 605a 0 605b 0 6064 0 6065 0
  //   6066 0 6067 0 6068 0 6069 0 606a 0 6075 0 6076 0 6077 0 6078 0 6079 0 6086 0 6087 0 6088 0 10d0 0
  //   6096 0 6097 0 6098 0 60a6 0 60a7 0 60a8 0 60b6 0 60b7 0 60b8 0 60c5 0 60c6 0 60c7 0 60c8 0 60c9 0
  //   f000
endmodule

module Unit15 (
  input  [7:0] Address,
  output [15:0] Instruction
);

  ROM #(.dataWidth(16)) rom_1 (.addr(Address), .data(Instruction));

  // Notes on the sheet:
  //   contents of rom_1 (hex, n*v repeats v):
  //   10a8 0 6014 0 6015 0 6016 0 6017 0 6018 0 6019 0 601a 0 6023 0 6024 0 6025 0 6026 0 6027 0 6028 0
  //   6029 0 602a 0 602b 0 6032 0 6033 0 6034 0 6036 0 6038 0 6039 0 603a 0 603b 0 603c 0 6041 0 6042 0
  //   6043 0 6044 0 6045 0 6046 0 6047 0 6048 0 6049 0 604a 0 604b 0 604c 0 604d 0 6052 0 6053 0 6054 0
  //   6055 0 6056 0 6057 0 6058 0 6059 0 605a 0 605b 0 605c 0 6063 0 6064 0 6065 0 6066 0 6067 0 6068 0
  //   6069 0 606a 0 606b 0 6074 0 6075 0 6076 0 6077 0 6078 0 6079 0 607a 0 1030 0 6035 0 6037 0 6086 0
  //   6087 0 6088 0 10d0 0 6096 0 6097 0 6098 0 60a6 0 60a7 0 60a8 0 60b5 0 60b6 0 60b7 0 60b8 0 60b9 0
  //   60c5 0 60c6 0 60c7 0 60c8 0 60c9 0 f000
endmodule

module Unit16 (
  input  [7:0] Address,
  output [15:0] Instruction
);

  ROM #(.dataWidth(16)) rom_1 (.addr(Address), .data(Instruction));

  // Notes on the sheet:
  //   contents of rom_1 (hex, n*v repeats v):
  //   102c 0 6017 0 6026 0 6027 0 6028 0 6035 0 6036 0 6037 0 6038 0 6039 0 6044 0 6045 0 6046 0 6047 0
  //   6048 0 6049 0 604a 0 6053 0 6054 0 6055 0 6059 0 605a 0 605b 0 6062 0 6063 0 6064 0 606a 0 606b 0
  //   606c 0 6073 0 6074 0 6075 0 6079 0 607a 0 607b 0 6084 0 6085 0 6086 0 6087 0 6088 0 6089 0 608a 0
  //   6095 0 6096 0 6097 0 6098 0 6099 0 60a6 0 60a7 0 60a8 0 60b7 0 10c3 0 6056 0 6057 0 6058 0 6065 0
  //   6066 0 6067 0 6068 0 6069 0 6076 0 6077 0 6078 0 f000
endmodule

module Unit17 (
  input  [7:0] Address,
  output [15:0] Instruction
);

  ROM #(.dataWidth(16)) rom_1 (.addr(Address), .data(Instruction));

  // Notes on the sheet:
  //   contents of rom_1 (hex, n*v repeats v):
  //   10a0 0 6016 0 6017 0 6018 0 6024 0 6025 0 6029 0 602a 0 6033 0 603b 0 6042 0 604b 0 604c 0 6052 0
  //   605b 0 605c 0 6061 0 606c 0 6071 0 607c 0 6081 0 608c 0 6092 0 609b 0 609c 0 60a2 0 60ab 0 60ac 0
  //   60b3 0 60bb 0 60c4 0 60c5 0 60c9 0 60ca 0 60d6 0 60d7 0 60d8 0 10d0 0 6026 0 6027 0 6028 0 6034 0
  //   6035 0 6036 0 6037 0 6038 0 6039 0 603a 0 6043 0 6044 0 6049 0 604a 0 6053 0 605a 0 6062 0 606b 0
  //   6072 0 607b 0 6082 0 608b 0 6093 0 609a 0 60a3 0 60a4 0 60a9 0 60aa 0 60b4 0 60b5 0 60b6 0 60b7 0
  //   60b8 0 60b9 0 60ba 0 60c6 0 60c7 0 60c8 0 10e3 0 6045 0 6046 0 6047 0 6048 0 6054 0 6055 0 6056 0
  //   6057 0 6058 0 6059 0 6063 0 6064 0 6065 0 6066 0 6067 0 6068 0 6069 0 606a 0 6073 0 6074 0 6075 0
  //   6076 0 6078 0 6079 0 607a 0 6083 0 6084 0 6085 0 6086 0 6087 0 6088 0 6089 0 608a 0 6094 0 6095 0
  //   6096 0 6097 0 6098 0 6099 0 60a5 0 60a6 0 60a7 0 60a8 0 10c3 0 6077 0 f000
endmodule

module Unit18 (
  input  [7:0] Address,
  output [15:0] Instruction
);

  ROM #(.dataWidth(16)) rom_1 (.addr(Address), .data(Instruction));

  // Notes on the sheet:
  //   contents of rom_1 (hex, n*v repeats v):
  //   102c 0 6016 0 6017 0 6018 0 6019 0 6024 0 6025 0 602a 0 602b 0 6033 0 603b 0 6042 0 604c 0 6052 0
  //   605c 0 6061 0 606d 0 6071 0 607d 0 6081 0 608d 0 6092 0 609c 0 60a2 0 60ac 0 60b3 0 60bb 0 60c4 0
  //   60c5 0 60ca 0 60cb 0 60d6 0 60d7 0 60d8 0 60d9 0 1030 0 6026 0 6027 0 6028 0 6029 0 6034 0 6035 0
  //   6036 0 6038 0 6039 0 603a 0 6043 0 6044 0 6045 0 6048 0 6049 0 604a 0 604b 0 6053 0 6054 0 6055 0
  //   6056 0 6057 0 6058 0 6059 0 605a 0 605b 0 6062 0 6063 0 6065 0 6066 0 6067 0 6068 0 606a 0 606b 0
  //   606c 0 6072 0 6073 0 6074 0 6075 0 6076 0 6077 0 6078 0 6079 0 607a 0 607b 0 607c 0 6082 0 6083 0
  //   6085 0 6086 0 6087 0 6088 0 608a 0 608b 0 608c 0 6093 0 6094 0 6095 0 6096 0 6097 0 6098 0 6099 0
  //   609a 0 609b 0 60a3 0 60a4 0 60a5 0 60a8 0 60a9 0 60aa 0 60ab 0 60b4 0 60b5 0 60b6 0 60b8 0 60b9 0
  //   60ba 0 60c6 0 60c7 0 60c8 0 60c9 0 10c3 0 6037 0 6046 0 6047 0 6064 0 6069 0 6084 0 6089 0 60a6 0
  //   60a7 0 f000
endmodule

module Unit19 (
  input  [7:0] Address,
  output [15:0] Instruction
);

  ROM #(.dataWidth(16)) rom_1 (.addr(Address), .data(Instruction));

  // Notes on the sheet:
  //   contents of rom_1 (hex, n*v repeats v):
  //   10c3 0 6007 0 6016 0 6017 0 6018 0 6026 0 6027 0 6028 0 6036 0 6037 0 6038 0 6046 0 6047 0 6048 0
  //   6056 0 6057 0 6058 0 6066 0 6067 0 6068 0 6076 0 6077 0 6078 0 6086 0 6087 0 6088 0 60b6 0 60b7 0
  //   60b8 0 60c6 0 60c7 0 60c8 0 60d6 0 60d7 0 60d8 0 60e5 0 60e6 0 60e7 0 60e8 0 60e9 0 10e3 0 6095 0
  //   6096 0 6097 0 6098 0 60a4 0 60a8 0 10a0 0 60a5 0 60a6 0 60a7 0 f000
endmodule

module Unit20 (
  input  [7:0] Address,
  output [15:0] Instruction
);

  ROM #(.dataWidth(16)) rom_1 (.addr(Address), .data(Instruction));

  // Notes on the sheet:
  //   contents of rom_1 (hex, n*v repeats v):
  //   10c3 0 6015 0 6016 0 6017 0 6018 0 6019 0 6023 0 6024 0 6025 0 6026 0 6027 0 6028 0 6029 0 602a 0
  //   602b 0 6032 0 6033 0 6034 0 603a 0 603b 0 603c 0 6041 0 6042 0 6043 0 604b 0 604c 0 604d 0 6051 0
  //   6052 0 605c 0 605d 0 6061 0 6062 0 606c 0 606d 0 6071 0 6072 0 6077 0 6078 0 6079 0 607c 0 607d 0
  //   6081 0 6082 0 6086 0 6087 0 6088 0 6089 0 608c 0 608d 0 6091 0 6092 0 6097 0 6098 0 6099 0 609c 0
  //   609d 0 60a1 0 60a2 0 60ac 0 60ad 0 60b1 0 60b2 0 60b3 0 60bb 0 60bc 0 60bd 0 60c2 0 60c3 0 60c4 0
  //   60ca 0 60cb 0 60cc 0 60d3 0 60d4 0 60d5 0 60d6 0 60d7 0 60d8 0 60d9 0 60da 0 60db 0 60e5 0 60e6 0
  //   60e7 0 60e8 0 60e9 0 f000
endmodule

module CU1 (
  input  [7:0] Opcode,
  input  ZeroFlag,
  output IR_Load,
  output RegB_Load,
  output ALU_Store,
  output [2:0] ALU_Op,
  output HLT,
  output PC_Inc,
  output RegA_Load,
  output RAM_WE,
  output PC_Load,
  output JZ_OUT,
  output VRAM_WE,
  output Inc,
  output VRAM_WE_B,
  output INC_B,
  output RAM_RE
);

  wire comparator_1_eq, comparator_2_eq, comparator_3_eq, comparator_4_eq, comparator_5_eq, comparator_6_eq,
       comparator_9_eq, comparator_10_eq, comparator_11_eq, not_1_out;

  Comparator #(.mode("unsigned")) comparator_1 (.a(Opcode), .b(8'h10), .eq(comparator_1_eq));  // open: gt, lt
  Comparator #(.mode("unsigned")) comparator_2 (.a(Opcode), .b(8'h11), .eq(comparator_2_eq));  // open: gt, lt
  Comparator #(.mode("unsigned")) comparator_3 (.a(Opcode), .b(8'h20), .eq(comparator_3_eq));  // open: gt, lt
  Comparator #(.mode("unsigned")) comparator_4 (.a(Opcode), .b(8'h21), .eq(comparator_4_eq));  // open: gt, lt
  Comparator #(.mode("unsigned")) comparator_5 (.a(Opcode), .b(8'h22), .eq(comparator_5_eq));  // open: gt, lt
  Comparator #(.mode("unsigned")) comparator_6 (.a(Opcode), .b(8'h23), .eq(comparator_6_eq));  // open: gt, lt
  Comparator #(.mode("unsigned")) comparator_7 (.a(Opcode), .b(8'hf0), .eq(HLT));  // open: gt, lt
  Comparator #(.mode("unsigned")) comparator_8 (.a(Opcode), .b(8'h30), .eq(RAM_WE));  // open: gt, lt
  Comparator #(.mode("unsigned")) comparator_9 (.a(Opcode), .b(8'h40), .eq(comparator_9_eq));  // open: gt, lt
  Comparator #(.mode("unsigned")) comparator_10 (.a(Opcode), .b(8'h50), .eq(comparator_10_eq));  // open: gt, lt
  Comparator #(.mode("unsigned")) comparator_11 (.a(Opcode), .b(8'h60), .eq(comparator_11_eq));  // open: gt, lt
  Comparator #(.mode("unsigned")) comparator_12 (.a(Opcode), .b(8'h70), .eq(Inc));  // open: gt, lt
  Comparator #(.mode("unsigned")) comparator_13 (.a(Opcode), .b(8'h61), .eq(VRAM_WE_B));  // open: gt, lt
  Comparator #(.mode("unsigned")) comparator_14 (.a(Opcode), .b(8'h71), .eq(INC_B));  // open: gt, lt
  Comparator #(.mode("unsigned")) comparator_15 (.a(Opcode), .b(8'h80), .eq(RAM_RE));  // open: gt, lt
  not not_1 (not_1_out, HLT);
  and and_1 (JZ_OUT, comparator_10_eq, ZeroFlag);
  or or_1 (ALU_Op[1], comparator_5_eq, comparator_6_eq);
  or or_2 (PC_Load, comparator_9_eq, JZ_OUT);
  or or_3 (VRAM_WE, comparator_11_eq, VRAM_WE_B);
  or or_4 (ALU_Op[0], comparator_4_eq, comparator_6_eq);
  and and_2 (PC_Inc, 1'b1, not_1_out);
  or or_5 (RegB_Load, comparator_2_eq, INC_B);
  or or_6 (ALU_Store, comparator_3_eq, comparator_6_eq, Inc, comparator_5_eq, comparator_5_eq);
  or or_7 (RegA_Load, comparator_1_eq, comparator_3_eq, comparator_5_eq, comparator_5_eq, comparator_6_eq, Inc, RAM_RE);

  assign ALU_Op[2] = 1'b0;
  assign IR_Load = 1'b1;

  // Notes on the sheet:
  //   1
  //   2
  //   3
  //   4
  //   5
  //   6
  //   7
  //   9
  //   12
  //   13
  //   14
  //   15
  //   8
  //   10
  //   11
endmodule

module LEDS (
  input  in_1
);

  // Switch switch_1: pin names not known
  // RGBLED rgbled_1: pin names not known; wires that end beside it: in_1
  // RGBLED rgbled_2: pin names not known; wires that end beside it: in_1
endmodule
